# Fritzing sketch try-me-leds (saved by Fritzing 1.0.2b)

parts:
  Bauteil1 = Arduino Uno (Rev3)
  Bauteil2 = Arduino Uno (Rev3)
  RGB_SMD_LED1 = SMD RGB LED (WS2812) [package=5050]
  S1 = SPST Switch [package=switch-spdt-smd]
  Bauteil3 = JeePlug experimenter's board

nets:
  N1: Bauteil1.D3_PWM, S1.O
  N2: Bauteil1.5V, Bauteil3.N$39
  N3: Bauteil1.GND, Bauteil3.N$21
  N4: Bauteil2.D3_PWM, S1.P
  N5: Bauteil2.5V, Bauteil3.N$31
  N6: Bauteil2.GND, Bauteil3.N$64
  N7: RGB_SMD_LED1.DOut, Bauteil3.N$37
  N8: RGB_SMD_LED1.DIn, S1.S
  N9: RGB_SMD_LED1.VCC, Bauteil3.N$47
